// Logisim project Acionamento_Motor.circ as structural Verilog: 2 circuits, main circuit main
module main (
  input  Sensor_IR
);

  wire A___Betoneira_Local_out, acionamento_1_lampada, acionamento_1_motor, B___Betoneira_Remota_out;

  Button B___Betoneira_Remota (.out(B___Betoneira_Remota_out));
  Button A___Betoneira_Local (.out(A___Betoneira_Local_out));
  Acionamento acionamento_1 (
    .A(A___Betoneira_Local_out), .B(B___Betoneira_Remota_out), .C___Sensor_IR(Sensor_IR),
    .Lampada(acionamento_1_lampada), .Motor(acionamento_1_motor));
  LED Lampada (.in(acionamento_1_lampada));
  LED Motor (.in(acionamento_1_motor));
endmodule

module Acionamento (
  input  A,
  input  B,
  input  C___Sensor_IR,
  output Lampada,
  output Motor
);

  or or_1 (Lampada, B, A);
  and and_1 (Motor, Lampada, C___Sensor_IR);
endmodule
