// Logisim project Dado_Eletrônico.circ as structural Verilog: 2 circuits, main circuit main
module main (
);

  wire clock_1_out, dado_1_l1, dado_1_l2, dado_1_l3, dado_1_l4, dado_1_l5, dado_1_l6, dado_1_l7;
  wire [2:0] random_1_out;

  Clock clock_1 (.out(clock_1_out));
  Random #(.width(3)) random_1 (.clk(clock_1_out), .out(random_1_out));  // open: next, clr
  dado dado_1 (
    .in_1(random_1_out), .L1(dado_1_l1), .L2(dado_1_l2), .L3(dado_1_l3), .L4(dado_1_l4), .L5(dado_1_l5),
    .L6(dado_1_l6), .L7(dado_1_l7));
  LED led_1 (.in(dado_1_l1));
  LED led_2 (.in(dado_1_l2));
  LED led_3 (.in(dado_1_l3));
  LED led_4 (.in(dado_1_l5));
  LED led_5 (.in(dado_1_l4));
  LED led_6 (.in(dado_1_l6));
  LED led_7 (.in(dado_1_l7));
endmodule

module dado (
  input  [2:0] in_1,
  output L1,
  output L2,
  output L3,
  output L4,
  output L5,
  output L6,
  output L7
);

  or or_1 (L1, in_1[2], in_1[1]);
  and and_1 (L2, in_1[2], in_1[1]);

  assign L3 = in_1[2];
  assign L4 = in_1[0];
  assign L5 = in_1[2];
  assign L6 = L2;
  assign L7 = L1;
endmodule
