// Logisim project Exercicio_01.circ as structural Verilog: 2 circuits, main circuit main
module main (
  input  A,
  input  B,
  input  C,
  input  A_2,
  input  B_2,
  input  C_2,
  output S,
  output S_2
);

  wire and_1_out, and_2_out, and_3_out, and_4_out, and_5_out, and_6_out, not_1_out, not_2_out, not_3_out,
       not_4_out, not_5_out, not_6_out, not_7_out, not_8_out;

  not not_1 (not_1_out, A);
  not not_2 (not_2_out, B);
  not not_3 (not_3_out, C);
  not not_4 (not_4_out, A);
  not not_5 (not_5_out, B);
  not not_6 (not_6_out, A);
  and and_1 (and_1_out, not_1_out, not_2_out, not_3_out);
  and and_2 (and_2_out, not_4_out, not_5_out, C);
  and and_3 (and_3_out, not_6_out, B, C);
  and and_4 (and_4_out, A, B, C);
  or or_1 (S, and_1_out, and_2_out, and_3_out, and_4_out);
  not not_7 (not_7_out, A_2);
  not not_8 (not_8_out, B_2);
  and and_5 (and_5_out, not_7_out, not_8_out);
  and and_6 (and_6_out, B_2, C_2);
  or or_2 (S_2, and_5_out, and_6_out);
endmodule

module simplificado (
  input  A,
  input  B,
  input  C,
  output S
);

  wire and_1_out, and_2_out, not_1_out, not_2_out;

  not not_1 (not_1_out, A);
  not not_2 (not_2_out, B);
  and and_1 (and_1_out, not_1_out, not_2_out);
  and and_2 (and_2_out, B, C);
  or or_1 (S, and_1_out, and_2_out);
endmodule
