// Logisim project circuitos_01.circ as structural Verilog
module Add_1 (
  input  A,
  input  B,
  input  C,
  output out_4,
  output out_5
);

  wire and_1_out, and_2_out, or_1_out, xor_1_out;

  or or_1 (or_1_out, C, B);
  xor xor_1 (xor_1_out, A, B);
  and and_1 (and_1_out, C, B);
  xor xor_2 (out_5, xor_1_out, C);
  and and_2 (and_2_out, or_1_out, A);
  or or_2 (out_4, and_2_out, and_1_out);
endmodule

module Add_4 (
  input  [3:0] B,
  input  [3:0] A,
  output out_3,
  output [3:0] S
);

  wire add_1_1_p4, add_1_2_p6, add_1_3_p6;

  // Add_1 add_1_1: pin names not known; wires that end beside it: out_3, A[3], B[3], add_1_1_p4, add_1_1_p4
  // Add_1 add_1_2: pin names not known; wires that end beside it: add_1_1_p4, add_1_1_p4, A[2], S[2], B[2], add_1_2_p6, add_1_2_p6
  // Add_1 add_1_3: pin names not known; wires that end beside it: add_1_2_p6, add_1_2_p6, A[1], S[1], B[1], add_1_3_p6, add_1_3_p6
  // Add_1 add_1_4: pin names not known; wires that end beside it: add_1_3_p6, add_1_3_p6, A[0], S[0], B[0], 1'b0
endmodule
